# Fritzing sketch plans (saved by Fritzing 1.0.5)

parts:
  DS1 = DS18B20 1-Wire Temperature Sensor [part_number=DS18B20]
  Grove1 = Grove OLED 128x96
  DS2 = DS18B20 1-Wire Temperature Sensor [part_number=DS18B20]
  DS3 = DS18B20 1-Wire Temperature Sensor [part_number=DS18B20]
  R1 = Resistor [tolerance=±5% power=0.25W resistance=220 package=THT]
  U1 = ESP32-38PinWide [part_number=ESP32-38PinWide]

nets:
  GND: DS1.GND, Grove1.GND, DS2.GND, DS3.GND, U1.GND
  N1: DS1.DQ, DS2.DQ, R1.Pin_1
  VDD: DS1.VDD, DS2.VDD, R1.Pin_0
  VCC: Grove1.VCC, DS3.VDD, U1.3.3
  N2: Grove1.SDA, U1.GPIO1
  N3: Grove1.SCL, U1.GPIO22
  N4: DS3.DQ, U1.GPIO16

custom parts:
  ESP32-38PinWide: Generic 38-Pin ESP32 with wide format (only access to one side of pins on a breadboard) based on Stephen Lilley's HiLetgo ESP-WROOM-32 ESP32 ESP-32S Development Board.
